# Fritzing sketch schematic (saved by Fritzing 0.9.3b)
breadboards: 1

parts:
  MCU1 = Raspberry Pi Zero
  IC1 = MCP3008 [part_number=MCP3008]
  Part1 = Soil Moisture Sensor

nets:
  N1: MCU1.pin_1, MCU1.pin_17, IC1.connector15, IC1.connector16
  N2: MCU1.pin_6, MCU1.pin_34, MCU1.pin_39, IC1.connector9, IC1.connector14, Part1.GND
  N3: MCU1.pin_12, IC1.connector13
  N4: MCU1.pin_16, IC1.connector12
  N5: MCU1.pin_18, IC1.connector11
  N6: MCU1.pin_22, IC1.connector10
  N7: MCU1.pin_38, Part1.VCC
  N8: IC1.connector1, Part1.SIG
